# Fritzing sketch sketch-12-2 (saved by Fritzing 0.9.2b)
circuit board: 8.46667cm x 5.64444cm
breadboards: 1

parts:
  Part1 = Arduino Leonardo (Rev3b)
  R1 = Resistor [tolerance=±5% resistance=220 package=THT]
  LED1 = LED - 5mm [color="Red (633nm)" package="5 mm [THT]"]
  S1 = Pushbutton [package="[THT]"]
  R2 = Resistor [tolerance=±5% resistance=10k package=THT]

nets:
  N1: Part1.5V, S1.Pin_3, S1.Pin_4
  N2: Part1.GND, LED1.cathode, R2.Pin_1
  N3: Part1.D8/A8, S1.Pin_1, S1.Pin_2, R2.Pin_0
  N4: Part1.D13_PWM, R1.Pin_0
  N5: R1.Pin_1, LED1.anode
